# Fritzing sketch LED (saved by Fritzing 0.9.6b)
breadboards: 1

parts:
  MCU1 = Raspberry Pi Zero
  LED1 = LED - 3mm [color="Red (633nm)" current=0.030 package="3 mm [THT]"]
  LED2 = LED - 3mm [color="Yellow (595nm)" current=0.030 package="3 mm [THT]"]
  LED3 = LED - 3mm [color="Blue (525nm)" current=0.030 package="3 mm [THT]"]
  LED4 = LED - 3mm [color="White (4500K)" current=0.030 package="3 mm [THT]"]
  R1 = Resistor [tolerance=±5% resistance=220 package="2010 [SMD]"]
  R2 = Resistor [tolerance=±5% resistance=220 package="2010 [SMD]"]
  R3 = Resistor [tolerance=±5% resistance=220 package="2010 [SMD]"]
  R4 = Resistor [tolerance=±5% resistance=220 package="2010 [SMD]"]

nets:
  N1: MCU1.pin_6, MCU1.pin_30, MCU1.pin_39, R1.Pin_1, R2.Pin_1, R3.Pin_1, R4.Pin_1
  N2: MCU1.pin_11, LED1.cathode
  N3: MCU1.pin_15, LED2.cathode
  N4: MCU1.pin_19, LED3.cathode
  N5: MCU1.pin_23, LED4.cathode
  N6: LED1.anode, R1.Pin_0
  N7: LED2.anode, R2.Pin_0
  N8: LED3.anode, R3.Pin_0
  N9: LED4.anode, R4.Pin_0
