# Fritzing sketch Motor (saved by Fritzing 0.9.6b)
breadboards: 1

parts:
  MCU1 = Raspberry Pi Zero
  M1 = DC Motor
  M2 = DC Motor
  VCC1 = Battery
  DRV8835 = DRV8835 Dual Motor Driver Carrier

nets:
  N1: MCU1.pin_1, MCU1.pin_17, DRV8835.GND#14
  N2: MCU1.pin_11, DRV8835.BOUT2
  N3: MCU1.pin_15, DRV8835.BOUT1
  N4: MCU1.pin_19, DRV8835.AOUT2
  N5: MCU1.pin_21, M1.pin_1, DRV8835.BIN2/BENABLE, DRV8835.AOUT1
  N6: M1.pin_2, DRV8835.VCC
  N7: M2.pin_1, DRV8835.AIN2/AENABLE
  N8: M2.pin_2, DRV8835.BIN1/BPHASE
  N9: VCC1.-, DRV8835.MODE
  N10: VCC1.+, DRV8835.GND#0
