# Fritzing sketch multi_servo (saved by Fritzing 0.9.6b)

parts:
  J1 = Basic Servo
  J3 = Basic Servo
  PWM1 = PCA9685 16x12-bit PWM Breakout
  MCU1 = Raspberry Pi Zero
  VCC1 = 4 x AAA Battery Mount  # not connected
  J2 = Basic Servo

nets:
  N1: J1.pulse, PWM1.no_name_yet#11
  N2: J3.pulse, PWM1.no_name_yet#0
  N3: PWM1.no_name_yet#4, J2.pulse
  N4: PWM1.no_name_yet#100, PWM1.no_name_yet#104, PWM1.no_name_yet#111
  N5: PWM1.no_name_yet#601, PWM1.no_name_yet#1000, PWM1.no_name_yet#1004, PWM1.no_name_yet#1011, MCU1.pin_39
  N6: PWM1.no_name_yet#603, MCU1.pin_5
  N7: PWM1.no_name_yet#604, MCU1.pin_3
  N8: PWM1.no_name_yet#605, MCU1.pin_1
