# Fritzing sketch servo (saved by Fritzing 0.9.6b)
breadboards: 1

parts:
  VCC1 = 4 x AAA Battery Mount
  MCU1 = Raspberry Pi Zero
  J1 = Basic Servo

nets:
  N1: VCC1.-, MCU1.pin_9, MCU1.pin_39, J1.gnd
  N2: VCC1.+, J1.vcc
  N3: MCU1.pin_1, J1.pulse
